// Logisim project imm-gen.circ as structural Verilog: 1 circuit, main circuit imm_gen
module imm_gen (
  input  [31:0] Instruction,
  input  [2:0] ImmSel,
  output [31:0] Immediate
);

  wire [31:0] B_type, I_type, J_type, S_type, U_type;

  assign I_type = {{20{Instruction[31]}}, Instruction[31:20]};  // Bit_Extender bit_extender_1
  assign B_type = {{19{Instruction[31]}}, {Instruction[31], Instruction[7], Instruction[30:25], Instruction[11:8], 1'b0}};  // Bit_Extender bit_extender_2
  Multiplexer #(.select(3), .width(32)) multiplexer_1 (
    .in0(I_type), .in1(S_type), .in2(B_type), .in3(U_type), .in4(J_type), .out(Immediate), .sel(ImmSel));  // open: in5, in6, in7

  // Notes on the sheet:
  //   INPUTS to your circuit
  //   DON'T CHANGE THE LOCATIONS OF THE INPUTS AND OUTPUTS!
  //   OUTPUT from your circuit
endmodule
