// Logisim project partial-load.circ as structural Verilog: 1 circuit, main circuit partial_load
module partial_load (
  input  [31:0] Instruction,
  input  [31:0] MemAddress,
  input  [31:0] DataFromMem,
  output [31:0] DataToReg
);

  wire comparator_1_eq, comparator_2_eq, comparator_2_gt, comparator_2_lt, is_lb, is_lh, is_lw;
  wire [1:0] offset;
  wire [7:0] multiplexer_2_out;
  wire [15:0] multiplexer_1_out;
  wire [31:0] and_4_out, and_5_out, and_6_out, bit_extender_4_out, bit_extender_5_out, bit_extender_6_out,
       \byte , halfword;

  Bit_Extender #(.in_width(32), .out_width(2)) bit_extender_1 (.in(MemAddress), .out(offset));
  Multiplexer #(.select(2), .width(16)) multiplexer_1 (
    .in0(DataFromMem[15:0]), .in1(DataFromMem[23:8]), .in2(DataFromMem[31:16]), .out(multiplexer_1_out),
    .sel(offset));  // open: in3
  Multiplexer #(.select(2), .width(8)) multiplexer_2 (
    .in0(DataFromMem[7:0]), .in1(DataFromMem[15:8]), .in2(DataFromMem[23:16]), .in3(DataFromMem[31:24]),
    .out(multiplexer_2_out), .sel(offset));
  assign halfword = {{16{multiplexer_1_out[15]}}, multiplexer_1_out};  // Bit_Extender bit_extender_2
  assign \byte  = {{24{multiplexer_2_out[7]}}, multiplexer_2_out};  // Bit_Extender bit_extender_3
  Comparator #(.width(7)) comparator_1 (.a(Instruction[6:0]), .b(7'b0000011), .eq(comparator_1_eq));  // open: gt, lt
  Comparator #(.width(3)) comparator_2 (
    .a(Instruction[14:12]), .b(3'b001), .gt(comparator_2_gt), .eq(comparator_2_eq), .lt(comparator_2_lt));
  assign bit_extender_4_out = {{31{is_lb}}, is_lb};  // Bit_Extender bit_extender_4
  assign bit_extender_5_out = {{31{is_lh}}, is_lh};  // Bit_Extender bit_extender_5
  assign bit_extender_6_out = {{31{is_lw}}, is_lw};  // Bit_Extender bit_extender_6
  and and_1 (is_lw, comparator_1_eq, comparator_2_gt);
  and and_2 (is_lh, comparator_1_eq, comparator_2_eq);
  and and_3 (is_lb, comparator_1_eq, comparator_2_lt);
  assign and_4_out = \byte  & bit_extender_4_out;  // AND_Gate and_4, 32 bits wide
  assign and_5_out = halfword & bit_extender_5_out;  // AND_Gate and_5, 32 bits wide
  assign and_6_out = DataFromMem & bit_extender_6_out;  // AND_Gate and_6, 32 bits wide
  assign DataToReg = and_4_out | and_5_out | and_6_out;  // OR_Gate or_1, 32 bits wide

  // Other names for the same wires on the sheet: word[31:0] = DataFromMem; opcode[6:0] = Instruction[6:0];
  //   funct3[2:0] = Instruction[14:12]

  // Notes on the sheet:
  //   INPUTS to your circuit
  //   DON'T CHANGE THE LOCATIONS OF THE INPUTS AND OUTPUTS!
  //   OUTPUT from your circuit
endmodule
