// Logisim project ex4.circ as structural Verilog: 5 circuits, main circuit RotRight
module RotRight (
  input  [15:0] INPUT0,
  input  [3:0] AMOUNT,
  output [15:0] OUTPUT0
);

  wire [15:0] tun1, tun2, tun3, tun4, tun5, tun6, tun7, tun8, tun9, tun10, tun11, tun12, tun13, tun14, tun15;

  rot1 rot1_1 (.out_2(tun1), .in_1(INPUT0));
  rot2 rot2_1 (.out_2(tun2), .in_1(INPUT0));
  rot4 rot4_1 (.out_2(tun4), .in_1(INPUT0));
  rot8 rot8_1 (.out_2(tun8), .in_1(INPUT0));
  rot2 rot2_2 (.out_2(tun3), .in_1(tun1));
  rot2 rot2_3 (.out_2(tun6), .in_1(tun4));
  rot1 rot1_2 (.out_2(tun9), .in_1(tun8));
  rot2 rot2_4 (.out_2(tun10), .in_1(tun8));
  rot4 rot4_2 (.out_2(tun12), .in_1(tun8));
  rot4 rot4_3 (.out_2(tun7), .in_1(tun3));
  rot2 rot2_5 (.out_2(tun5), .in_1(tun3));
  rot4 rot4_4 (.out_2(tun13), .in_1(tun9));
  rot1 rot1_3 (.out_2(tun11), .in_1(tun10));
  rot4 rot4_5 (.out_2(tun14), .in_1(tun10));
  Multiplexer #(.enable("false"), .select(4), .width(16)) multiplexer_1 (
    .in0(INPUT0), .in1(tun1), .in2(tun2), .in3(tun3), .in4(tun4), .in5(tun5), .in6(tun6), .in7(tun7),
    .in8(tun8), .in9(tun9), .in10(tun10), .in11(tun11), .in12(tun12), .in13(tun13), .in14(tun14),
    .in15(tun15), .out(OUTPUT0), .sel(AMOUNT));
  rot8 rot8_2 (.out_2(tun15), .in_1(tun7));

  // Other names for the same wires on the sheet: sel[3:0] = AMOUNT; tun0[15:0] = INPUT0
endmodule

module rot1 (
  input  [15:0] in_1,
  output [15:0] out_2
);


  assign out_2 = {in_1[0], in_1[15:1]};
endmodule

module rot2 (
  input  [15:0] in_1,
  output [15:0] out_2
);

  wire [15:0] rot1_1_out_2;

  rot1 rot1_1 (.out_2(rot1_1_out_2), .in_1(in_1));
  rot1 rot1_2 (.out_2(out_2), .in_1(rot1_1_out_2));
endmodule

module rot4 (
  input  [15:0] in_1,
  output [15:0] out_2
);

  wire [15:0] rot2_1_out_2;

  rot2 rot2_1 (.out_2(rot2_1_out_2), .in_1(in_1));
  rot2 rot2_2 (.out_2(out_2), .in_1(rot2_1_out_2));
endmodule

module rot8 (
  input  [15:0] in_1,
  output [15:0] out_2
);

  wire [15:0] rot4_1_out_2;

  rot4 rot4_1 (.out_2(rot4_1_out_2), .in_1(in_1));
  rot4 rot4_2 (.out_2(out_2), .in_1(rot4_1_out_2));
endmodule
